// Logisim project NTT_ALU.circ as structural Verilog: 5 circuits, main circuit HalfAdder
// NTT_HalfAdder
module HalfAdder (
  input  A,
  input  B,
  output Sum,
  output Carry
);

  Xor xor_1 (.in_1(A), .in_2(B), .out_3(Sum));
  And and_1 (.in_1(A), .in_2(B), .out_3(Carry));
endmodule

// NTT_FullAdder
module FullAdder (
  input  A,
  input  B,
  input  C,
  output Sum,
  output Carry
);

  wire halfadder_1_carry, halfadder_1_sum, halfadder_2_carry;

  HalfAdder halfadder_1 (.A(A), .B(B), .Sum(halfadder_1_sum), .Carry(halfadder_1_carry));
  HalfAdder halfadder_2 (.A(halfadder_1_sum), .B(C), .Sum(Sum), .Carry(halfadder_2_carry));
  Or or_1 (.in_1(halfadder_2_carry), .in_2(halfadder_1_carry), .out_3(Carry));
endmodule

// NTT_Add16
module Add16 (
  input  [15:0] in_1,
  input  [15:0] in_2,
  output [15:0] out_3
);

  wire fulladder_1_carry, fulladder_2_carry, fulladder_3_carry, fulladder_4_carry, fulladder_5_carry,
       fulladder_6_carry, fulladder_7_carry, fulladder_8_carry, fulladder_9_carry, fulladder_10_carry,
       fulladder_11_carry, fulladder_12_carry, fulladder_13_carry, fulladder_14_carry, halfadder_1_carry;

  HalfAdder halfadder_1 (.A(in_1[0]), .B(in_2[0]), .Sum(out_3[0]), .Carry(halfadder_1_carry));
  FullAdder fulladder_1 (.A(halfadder_1_carry), .B(in_1[1]), .C(in_2[1]), .Sum(out_3[1]), .Carry(fulladder_1_carry));
  FullAdder fulladder_2 (.A(fulladder_1_carry), .B(in_1[2]), .C(in_2[2]), .Sum(out_3[2]), .Carry(fulladder_2_carry));
  FullAdder fulladder_3 (.A(fulladder_2_carry), .B(in_1[3]), .C(in_2[3]), .Sum(out_3[3]), .Carry(fulladder_3_carry));
  FullAdder fulladder_4 (.A(fulladder_3_carry), .B(in_1[4]), .C(in_2[4]), .Sum(out_3[4]), .Carry(fulladder_4_carry));
  FullAdder fulladder_5 (.A(fulladder_4_carry), .B(in_1[5]), .C(in_2[5]), .Sum(out_3[5]), .Carry(fulladder_5_carry));
  FullAdder fulladder_6 (.A(fulladder_5_carry), .B(in_1[6]), .C(in_2[6]), .Sum(out_3[6]), .Carry(fulladder_6_carry));
  FullAdder fulladder_7 (.A(fulladder_6_carry), .B(in_1[7]), .C(in_2[7]), .Sum(out_3[7]), .Carry(fulladder_7_carry));
  FullAdder fulladder_8 (.A(fulladder_7_carry), .B(in_1[8]), .C(in_2[8]), .Sum(out_3[8]), .Carry(fulladder_8_carry));
  FullAdder fulladder_9 (.A(fulladder_8_carry), .B(in_1[9]), .C(in_2[9]), .Sum(out_3[9]), .Carry(fulladder_9_carry));
  FullAdder fulladder_10 (
    .A(fulladder_9_carry), .B(in_1[10]), .C(in_2[10]), .Sum(out_3[10]), .Carry(fulladder_10_carry));
  FullAdder fulladder_11 (
    .A(fulladder_10_carry), .B(in_1[11]), .C(in_2[11]), .Sum(out_3[11]), .Carry(fulladder_11_carry));
  FullAdder fulladder_12 (
    .A(fulladder_11_carry), .B(in_1[12]), .C(in_2[12]), .Sum(out_3[12]), .Carry(fulladder_12_carry));
  FullAdder fulladder_13 (
    .A(fulladder_12_carry), .B(in_1[13]), .C(in_2[13]), .Sum(out_3[13]), .Carry(fulladder_13_carry));
  FullAdder fulladder_14 (
    .A(fulladder_13_carry), .B(in_1[14]), .C(in_2[14]), .Sum(out_3[14]), .Carry(fulladder_14_carry));
  FullAdder fulladder_15 (.A(fulladder_14_carry), .B(in_1[15]), .C(in_2[15]), .Sum(out_3[15]));  // open: Carry
endmodule

// NTT_ALU
module ALU (
  input  ZeroX,
  input  NegateX,
  input  ZeroY,
  input  NegateY,
  input  Add_And,
  input  NegateOut,
  input  [15:0] X,
  input  [15:0] Y,
  output [15:0] OUT,
  output Zero,
  output Negative
);

  wire or8way_1_out_9, or8way_2_out_9, or_1_out_3;
  wire [15:0] add16_1_out_3, and16_1_out_3, mux16_1_out_4, mux16_2_out_4, mux16_3_out_4, mux16_4_out_4,
       mux16_5_out_4, not16_1_out_2, not16_2_out_2, not16_3_out_2;

  Mux16 mux16_1 (.A(X), .B({16{1'b0}}), .Sel(ZeroX), .out_4(mux16_1_out_4));
  Mux16 mux16_2 (.A(Y), .B({16{1'b0}}), .Sel(ZeroY), .out_4(mux16_2_out_4));
  Not16 not16_1 (.in_1(mux16_1_out_4), .out_2(not16_1_out_2));
  Not16 not16_2 (.in_1(mux16_2_out_4), .out_2(not16_2_out_2));
  Mux16 mux16_3 (.A(mux16_1_out_4), .B(not16_1_out_2), .Sel(NegateX), .out_4(mux16_3_out_4));
  Mux16 mux16_4 (.A(mux16_2_out_4), .B(not16_2_out_2), .Sel(NegateY), .out_4(mux16_4_out_4));
  And16 and16_1 (.in_1(mux16_3_out_4), .in_2(mux16_4_out_4), .out_3(and16_1_out_3));
  Add16 add16_1 (.in_1(mux16_3_out_4), .in_2(mux16_4_out_4), .out_3(add16_1_out_3));
  Mux16 mux16_5 (.A(and16_1_out_3), .B(add16_1_out_3), .Sel(Add_And), .out_4(mux16_5_out_4));
  Not16 not16_3 (.in_1(mux16_5_out_4), .out_2(not16_3_out_2));
  Mux16 mux16_6 (.A(mux16_5_out_4), .B(not16_3_out_2), .Sel(NegateOut), .out_4({Negative, OUT[14:0]}));
  Or8Way or8way_1 (
    .in_1(OUT[8]), .in_2(OUT[9]), .in_3(OUT[10]), .in_4(OUT[11]), .in_5(OUT[12]), .in_6(OUT[13]),
    .in_7(OUT[14]), .in_8(Negative), .out_9(or8way_1_out_9));
  Or8Way or8way_2 (
    .in_1(OUT[0]), .in_2(OUT[1]), .in_3(OUT[2]), .in_4(OUT[3]), .in_5(OUT[4]), .in_6(OUT[5]), .in_7(OUT[6]),
    .in_8(OUT[7]), .out_9(or8way_2_out_9));
  Or or_1 (.in_1(or8way_2_out_9), .in_2(or8way_1_out_9), .out_3(or_1_out_3));
  Not not_1 (.in_1(or_1_out_3), .out_2(Zero));

  assign OUT[15] = Negative;
endmodule

// NTT_Inc16
module Inc16 (
  input  [15:0] in_1,
  output [15:0] out_2
);

  wire halfadder_1_carry, halfadder_2_carry, halfadder_3_carry, halfadder_4_carry, halfadder_5_carry,
       halfadder_6_carry, halfadder_7_carry, halfadder_8_carry, halfadder_9_carry, halfadder_10_carry,
       halfadder_11_carry, halfadder_12_carry, halfadder_13_carry, halfadder_14_carry, halfadder_15_carry;

  HalfAdder halfadder_1 (.A(in_1[0]), .B(1'b1), .Sum(out_2[0]), .Carry(halfadder_1_carry));
  HalfAdder halfadder_2 (.A(halfadder_1_carry), .B(in_1[1]), .Sum(out_2[1]), .Carry(halfadder_2_carry));
  HalfAdder halfadder_3 (.A(halfadder_2_carry), .B(in_1[2]), .Sum(out_2[2]), .Carry(halfadder_3_carry));
  HalfAdder halfadder_4 (.A(halfadder_3_carry), .B(in_1[3]), .Sum(out_2[3]), .Carry(halfadder_4_carry));
  HalfAdder halfadder_5 (.A(halfadder_4_carry), .B(in_1[4]), .Sum(out_2[4]), .Carry(halfadder_5_carry));
  HalfAdder halfadder_6 (.A(halfadder_5_carry), .B(in_1[5]), .Sum(out_2[5]), .Carry(halfadder_6_carry));
  HalfAdder halfadder_7 (.A(halfadder_6_carry), .B(in_1[6]), .Sum(out_2[6]), .Carry(halfadder_7_carry));
  HalfAdder halfadder_8 (.A(halfadder_7_carry), .B(in_1[7]), .Sum(out_2[7]), .Carry(halfadder_8_carry));
  HalfAdder halfadder_9 (.A(halfadder_8_carry), .B(in_1[8]), .Sum(out_2[8]), .Carry(halfadder_9_carry));
  HalfAdder halfadder_10 (.A(halfadder_9_carry), .B(in_1[9]), .Sum(out_2[9]), .Carry(halfadder_10_carry));
  HalfAdder halfadder_11 (.A(halfadder_10_carry), .B(in_1[10]), .Sum(out_2[10]), .Carry(halfadder_11_carry));
  HalfAdder halfadder_12 (.A(halfadder_11_carry), .B(in_1[11]), .Sum(out_2[11]), .Carry(halfadder_12_carry));
  HalfAdder halfadder_13 (.A(halfadder_12_carry), .B(in_1[12]), .Sum(out_2[12]), .Carry(halfadder_13_carry));
  HalfAdder halfadder_14 (.A(halfadder_13_carry), .B(in_1[13]), .Sum(out_2[13]), .Carry(halfadder_14_carry));
  HalfAdder halfadder_15 (.A(halfadder_14_carry), .B(in_1[14]), .Sum(out_2[14]), .Carry(halfadder_15_carry));
  HalfAdder halfadder_16 (.A(halfadder_15_carry), .B(in_1[15]), .Sum(out_2[15]));  // open: Carry
endmodule
