// Logisim project NTT_BasicGates.circ as structural Verilog: 15 circuits, main circuit And
// NTT_And
module And (
  input  in_1,
  input  in_2,
  output out_3
);

  wire nand_1_out;

  nand nand_1 (nand_1_out, in_1, in_2);
  Not NTT_NOT (.in_1(nand_1_out), .out_2(out_3));
endmodule

// NTT_Not
module Not (
  input  in_1,
  output out_2
);

  nand nand_1 (out_2, in_1, in_1);
endmodule

// NTT_Or
module Or (
  input  in_1,
  input  in_2,
  output out_3
);

  wire NTT_NOT_2_out_2, NTT_NOT_out_2;

  Not NTT_NOT (.in_1(in_1), .out_2(NTT_NOT_out_2));
  Not NTT_NOT_2 (.in_1(in_2), .out_2(NTT_NOT_2_out_2));
  nand nand_1 (out_3, NTT_NOT_out_2, NTT_NOT_2_out_2);
endmodule

// NTT_Xor
module Xor (
  input  in_1,
  input  in_2,
  output out_3
);

  wire nand_1_out, or_2_out_3;

  Or or_1 ();  // open: in_1, in_2, out_3
  nand nand_1 (nand_1_out, in_1, in_2);
  Or or_2 (.in_1(in_1), .in_2(in_2), .out_3(or_2_out_3));
  And and_1 (.in_1(nand_1_out), .in_2(or_2_out_3), .out_3(out_3));
endmodule

// NTT_Mux
module Mux (
  input  A,
  input  B,
  input  Sel,
  output out_4
);

  wire and_1_out_3, and_2_out_3, NTT_NOT_out_2;

  Not NTT_NOT (.in_1(Sel), .out_2(NTT_NOT_out_2));
  And and_1 (.in_1(B), .in_2(Sel), .out_3(and_1_out_3));
  And and_2 (.in_1(A), .in_2(NTT_NOT_out_2), .out_3(and_2_out_3));
  Or or_1 (.in_1(and_2_out_3), .in_2(and_1_out_3), .out_3(out_4));
endmodule

// NTT_DMux
module Dmux (
  input  In,
  input  Sel,
  output A,
  output B
);

  wire NTT_NOT_out_2;

  Not NTT_NOT (.in_1(Sel), .out_2(NTT_NOT_out_2));
  And NTT_AND (.in_1(In), .in_2(NTT_NOT_out_2), .out_3(A));
  And NTT_AND_2 (.in_1(In), .in_2(Sel), .out_3(B));
endmodule

// NTT_Not16
module Not16 (
  input  [15:0] in_1,
  output [15:0] out_2
);

  assign out_2 = ~(in_1 & in_1);  // NAND_Gate nand_1, 16 bits wide
endmodule

// NTT_And16
module And16 (
  input  [15:0] in_1,
  input  [15:0] in_2,
  output [15:0] out_3
);

  wire [15:0] nand_1_out;

  assign nand_1_out = ~(in_1 & in_2);  // NAND_Gate nand_1, 16 bits wide
  Not16 NTT_NOT16 (.in_1(nand_1_out), .out_2(out_3));
endmodule

// NTT_Or16
module Or16 (
  input  [15:0] in_1,
  input  [15:0] in_2,
  output [15:0] out_3
);

  wire [15:0] NTT_NOT16_2_out_2, NTT_NOT16_out_2;

  Not16 NTT_NOT16 (.in_1(in_1), .out_2(NTT_NOT16_out_2));
  Not16 NTT_NOT16_2 (.in_1(in_2), .out_2(NTT_NOT16_2_out_2));
  assign out_3 = ~(NTT_NOT16_out_2 & NTT_NOT16_2_out_2);  // NAND_Gate nand_1, 16 bits wide
endmodule

// NTT_Mux16
module Mux16 (
  input  [15:0] A,
  input  [15:0] B,
  input  Sel,
  output [15:0] out_4
);

  wire [15:0] NTT_AND16_2_out_3, NTT_AND16_out_3;
  wire [15:15] NTT_NOT_out_2;

  And16 NTT_AND16 (.in_1(A), .in_2({16{NTT_NOT_out_2[15]}}), .out_3(NTT_AND16_out_3));
  And16 NTT_AND16_2 (.in_1(B), .in_2({16{Sel}}), .out_3(NTT_AND16_2_out_3));
  Not NTT_NOT (.in_1(Sel), .out_2(NTT_NOT_out_2[15]));
  Or16 NTT_OR16 (.in_1(NTT_AND16_out_3), .in_2(NTT_AND16_2_out_3), .out_3(out_4));
endmodule

// NTT_Or8Way
module Or8Way (
  input  in_1,
  input  in_2,
  input  in_3,
  input  in_4,
  input  in_5,
  input  in_6,
  input  in_7,
  input  in_8,
  output out_9
);

  wire NTT_OR_2_out_3, NTT_OR_3_out_3, NTT_OR_4_out_3, NTT_OR_5_out_3, NTT_OR_6_out_3, NTT_OR_out_3;

  Or NTT_OR (.in_1(in_1), .in_2(in_2), .out_3(NTT_OR_out_3));
  Or NTT_OR_2 (.in_1(NTT_OR_out_3), .in_2(in_3), .out_3(NTT_OR_2_out_3));
  Or NTT_OR_3 (.in_1(NTT_OR_2_out_3), .in_2(in_4), .out_3(NTT_OR_3_out_3));
  Or NTT_OR_4 (.in_1(NTT_OR_3_out_3), .in_2(in_5), .out_3(NTT_OR_4_out_3));
  Or NTT_OR_5 (.in_1(NTT_OR_4_out_3), .in_2(in_6), .out_3(NTT_OR_5_out_3));
  Or NTT_OR_6 (.in_1(NTT_OR_5_out_3), .in_2(in_7), .out_3(NTT_OR_6_out_3));
  Or NTT_OR_7 (.in_1(NTT_OR_6_out_3), .in_2(in_8), .out_3(out_9));
endmodule

// NTT_Mux4Way16
module Mux4Way16 (
  input  [15:0] A,
  input  [15:0] B,
  input  Sel1,
  input  [15:0] C,
  input  [15:0] D,
  input  Sel2,
  output [15:0] Output
);

  wire [15:0] NTT_MUX16_2_out_4, NTT_MUX16_out_4;

  Mux16 NTT_MUX16 (.A(A), .B(B), .Sel(Sel1), .out_4(NTT_MUX16_out_4));
  Mux16 NTT_MUX16_2 (.A(C), .B(D), .Sel(Sel1), .out_4(NTT_MUX16_2_out_4));
  Mux16 NTT_MUX16_3 (.A(NTT_MUX16_out_4), .B(NTT_MUX16_2_out_4), .Sel(Sel2), .out_4(Output));
endmodule

// NTT_Mux8Way16
module Mux8Way16 (
  input  [15:0] A,
  input  [15:0] B,
  input  [15:0] C,
  input  [15:0] D,
  input  in_5,
  input  in_6,
  input  [15:0] E,
  input  in_8,
  input  [15:0] F,
  input  [15:0] G,
  input  [15:0] H,
  output [15:0] out_12
);

  wire [15:0] mux4way16_1_output, mux4way16_2_output;

  Mux4Way16 mux4way16_1 (.A(A), .B(B), .C(C), .D(D), .Sel1(in_5), .Sel2(in_6), .Output(mux4way16_1_output));
  Mux4Way16 mux4way16_2 (.A(E), .B(F), .C(G), .D(H), .Sel1(in_5), .Sel2(in_6), .Output(mux4way16_2_output));
  Mux16 NTT_MUX16 (.A(mux4way16_1_output), .B(mux4way16_2_output), .Sel(in_8), .out_4(out_12));
endmodule

// NTT_DMux4Way
module DMux4Way (
  input  in_1,
  input  in_2,
  input  in_3,
  output out_4,
  output out_5,
  output out_6,
  output out_7
);

  wire NTT_DMUX_a, NTT_DMUX_b;

  Dmux NTT_DMUX (.In(in_1), .Sel(in_2), .A(NTT_DMUX_a), .B(NTT_DMUX_b));
  Dmux NTT_DMUX_2 (.In(NTT_DMUX_a), .Sel(in_3), .A(out_4), .B(out_5));
  Dmux NTT_DMUX_3 (.In(NTT_DMUX_b), .Sel(in_3), .A(out_6), .B(out_7));
endmodule

// NTT_DMux8Way
module DMux8Way (
  input  in_1,
  input  in_2,
  input  in_3,
  input  in_4,
  output out_5,
  output out_6,
  output out_7,
  output out_8,
  output out_9,
  output out_10,
  output out_11,
  output out_12
);

  wire NTT_DMUX_a, NTT_DMUX_b;

  Dmux NTT_DMUX (.In(in_1), .Sel(in_2), .A(NTT_DMUX_a), .B(NTT_DMUX_b));
  DMux4Way dmux4way_1 (
    .in_1(NTT_DMUX_a), .in_3(in_3), .in_2(in_4), .out_4(out_5), .out_5(out_6), .out_6(out_7), .out_7(out_8));
  DMux4Way dmux4way_2 (
    .in_1(NTT_DMUX_b), .in_3(in_3), .in_2(in_4), .out_4(out_9), .out_5(out_10), .out_6(out_11), .out_7(out_12));
endmodule
