// Logisim project NTT_FullComputer.circ as structural Verilog: 5 circuits, main circuit FullMemory
// NTT_Memory
module FullMemory (
  input  Load,
  input  [15:0] In,
  input  [14:0] Addr,
  output [15:0] Out
);

  wire clock_1_out_1, dmux_1_a, dmux_1_b, dmux_2_a, dmux_2_b;
  wire [15:0] mux16_1_out_4, ram16k_1_out, ram_1_data, register_1_out_3;

  Dmux dmux_1 (.In(Load), .Sel(Addr[14]), .A(dmux_1_a), .B(dmux_1_b));
  Dmux dmux_2 (.In(dmux_1_b), .Sel(Addr[13]), .A(dmux_2_a), .B(dmux_2_b));
  RAM16k ram16k_1 (.Addr(Addr[13:0]), .In(In), .Load(dmux_1_a), .Out(ram16k_1_out));
  Clock clock_1 (.out_1(clock_1_out_1));
  Register register_1 (.in_1(In), .in_2(dmux_2_b), .out_3(register_1_out_3));
  RAM #(.addrWidth(13), .dataWidth(16), .bus("separate")) ram_1 (
    .addr(Addr[12:0]), .din(In), .data(ram_1_data), .str(dmux_2_a), .clk(clock_1_out_1), .ld(1'b1));  // open: sel, clr
  Mux16 mux16_1 (.A(ram_1_data), .B(register_1_out_3), .Sel(Addr[13]), .out_4(mux16_1_out_4));
  Mux16 mux16_2 (.A(ram16k_1_out), .B(mux16_1_out_4), .Sel(Addr[14]), .out_4(Out));
endmodule

// NTT_CPU
module CPU (
  input  [15:0] Instruction,
  input  [15:0] M_Input,
  input  reset,
  output WriteM,
  output [15:0] OutM,
  output [14:0] AddresM,
  output [15:0] PCOut
);

  wire alu_1_negative, alu_1_zero, and_1_out_3, and_2_out_3, and_3_out_3, not_1_out_2, not_2_out_2,
       not_3_out_2, or_1_out_3, or_2_out_3, or_3_out_3, or_4_out_3;
  wire [15:0] D_Register_out_3, mux16_1_out_4, mux16_2_out_4, mux16_3_out_4;
  wire [15:15] A_Register_out_3;

  Mux16 mux16_1 (
    .A({16{1'b0}}), .B(Instruction), .Sel(Instruction[15]),
    .out_4({mux16_1_out_4[15:4], WriteM, mux16_1_out_4[2:0]}));
  Mux16 mux16_2 (.A(OutM), .B(Instruction), .Sel(not_1_out_2), .out_4(mux16_2_out_4));
  Not not_1 (.in_1(Instruction[15]), .out_2(not_1_out_2));
  Register A_Register (.in_1(mux16_2_out_4), .in_2(or_1_out_3), .out_3({A_Register_out_3[15], AddresM}));
  Or or_1 (.in_1(mux16_1_out_4[5]), .in_2(not_1_out_2), .out_3(or_1_out_3));
  Register D_Register (.in_1(OutM), .in_2(mux16_1_out_4[4]), .out_3(D_Register_out_3));
  Mux16 mux16_3 (.A({A_Register_out_3[15], AddresM}), .B(M_Input), .Sel(mux16_1_out_4[12]), .out_4(mux16_3_out_4));
  ALU alu_1 (
    .X(D_Register_out_3), .Y(mux16_3_out_4), .ZeroX(mux16_1_out_4[11]), .NegateX(mux16_1_out_4[10]),
    .ZeroY(mux16_1_out_4[9]), .NegateY(mux16_1_out_4[8]), .Add_And(mux16_1_out_4[7]),
    .NegateOut(mux16_1_out_4[6]), .Zero(alu_1_zero), .Negative(alu_1_negative), .OUT(OutM));
  And and_1 (.in_1(mux16_1_out_4[1]), .in_2(alu_1_zero), .out_3(and_1_out_3));
  And and_2 (.in_1(mux16_1_out_4[2]), .in_2(alu_1_negative), .out_3(and_2_out_3));
  Or or_2 (.in_1(and_1_out_3), .in_2(and_2_out_3), .out_3(or_2_out_3));
  Or or_3 (.in_1(alu_1_negative), .in_2(alu_1_zero), .out_3(or_3_out_3));
  And and_3 (.in_1(not_3_out_2), .in_2(mux16_1_out_4[0]), .out_3(and_3_out_3));
  Or or_4 (.in_1(and_3_out_3), .in_2(or_2_out_3), .out_3(or_4_out_3));
  Not not_2 (.in_1(or_4_out_3), .out_2(not_2_out_2));
  Not not_3 (.in_1(or_3_out_3), .out_2(not_3_out_2));
  PCounter pcounter_1 (
    .In({A_Register_out_3[15], AddresM}), .Inc(not_2_out_2), .Load(or_4_out_3), .Reset(reset), .Out(PCOut));
endmodule

// NTT_Computer
module HackPC (
  input  in_1
);

  wire cpu_1_writem;
  wire [14:0] cpu_1_addresm;
  wire [15:0] cpu_1_outm, cpu_1_pcout, fullmemory_1_out, rom_1_data;

  ROM #(.addrWidth(16), .dataWidth(16)) rom_1 (.addr(cpu_1_pcout), .data(rom_1_data));  // open: sel
  CPU cpu_1 (
    .Instruction(rom_1_data), .M_Input(fullmemory_1_out), .reset(in_1), .WriteM(cpu_1_writem),
    .OutM(cpu_1_outm), .AddresM(cpu_1_addresm), .PCOut(cpu_1_pcout));
  FullMemory fullmemory_1 (.In(cpu_1_outm), .Addr(cpu_1_addresm), .Load(cpu_1_writem), .Out(fullmemory_1_out));

  // Notes on the sheet:
  //   contents of rom_1 (hex, n*v repeats v):
  //   1 fc10 3 e308 2 ea88 3 fc10 12 e302 0 fc10 2 f088 3 fc88 6 ea87 12 ea87 223
endmodule

module DebugHackPC (
  input  ResetCPU,
  input  Reset,
  input  jogar,
  input  _2Papel,
  input  _2Tesoura,
  input  _2Pedra,
  input  _1Papel,
  input  _1Tesoura,
  input  _1Pedra,
  output Processando,
  output Erro,
  output VitoriaP2,
  output Vitoria1,
  output Pontuacao2,
  output Pontuacao2_2,
  output Pontuacao1,
  output Pontuacao1_2
);

  wire alu_1_negative, alu_1_zero, and_1_out_3, and_2_out_3, and_3_out_3, and_5_out_3, clock_1_out_1,
       clock_2_out_1, clock_3_out_1, dmux_1_a, dmux_1_b, dmux_2_a, dmux_2_b, not_1_out_2, not_2_out_2,
       not_3_out_2, not_4_out_2, not_5_out_2, or_1_out_3, or_2_out_3, or_3_out_3, or_4_out_3, or_5_out_3,
       s_r_ff_1_qn;
  wire [6:6] and_4_out_3;
  wire [13:0] A_Register_out_3;
  wire [15:0] alu_1_out, D_Register_out_3, mux16_1_out_4, mux16_2_out_4, mux16_3_out_4, mux16_4_out_4,
       mux16_5_out_4, mux16_6_out_4, pcounter_1_out, ram_1_data, ram_2_data, register_1_out_3, rom_1_data;
  wire [15:14] A_Register_out_3_2;

  ROM #(.addrWidth(16), .dataWidth(16)) rom_1 (.addr(pcounter_1_out), .data(rom_1_data));  // open: sel
  Mux16 mux16_1 (.A({16{1'b0}}), .B(rom_1_data), .Sel(rom_1_data[15]), .out_4(mux16_1_out_4));
  Mux16 mux16_2 (.A(alu_1_out), .B(rom_1_data), .Sel(not_1_out_2), .out_4(mux16_2_out_4));
  Not not_1 (.in_1(rom_1_data[15]), .out_2(not_1_out_2));
  Register A_Register (.in_1(mux16_2_out_4), .in_2(or_1_out_3), .out_3({A_Register_out_3_2, A_Register_out_3}));
  Or or_1 (.in_1(mux16_1_out_4[5]), .in_2(not_1_out_2), .out_3(or_1_out_3));
  Register D_Register (.in_1(alu_1_out), .in_2(mux16_1_out_4[4]), .out_3(D_Register_out_3));
  Mux16 mux16_3 (
    .A({A_Register_out_3_2, A_Register_out_3}), .B(mux16_6_out_4), .Sel(mux16_1_out_4[12]),
    .out_4(mux16_3_out_4));
  And and_1 (.in_1(mux16_1_out_4[2]), .in_2(alu_1_negative), .out_3(and_1_out_3));
  ALU alu_1 (
    .X(D_Register_out_3), .Y(mux16_3_out_4), .ZeroX(mux16_1_out_4[11]), .NegateX(mux16_1_out_4[10]),
    .ZeroY(mux16_1_out_4[9]), .NegateY(mux16_1_out_4[8]), .Add_And(mux16_1_out_4[7]),
    .NegateOut(mux16_1_out_4[6]), .Zero(alu_1_zero), .Negative(alu_1_negative), .OUT(alu_1_out));
  And and_2 (.in_1(mux16_1_out_4[1]), .in_2(alu_1_zero), .out_3(and_2_out_3));
  Or or_2 (.in_1(and_2_out_3), .in_2(and_1_out_3), .out_3(or_2_out_3));
  Or or_3 (.in_1(alu_1_negative), .in_2(alu_1_zero), .out_3(or_3_out_3));
  And and_3 (.in_1(not_3_out_2), .in_2(mux16_1_out_4[0]), .out_3(and_3_out_3));
  Or or_4 (.in_1(and_3_out_3), .in_2(or_2_out_3), .out_3(or_4_out_3));
  Not not_2 (.in_1(or_4_out_3), .out_2(not_2_out_2));
  PCounter pcounter_1 (
    .In({A_Register_out_3_2, A_Register_out_3}), .Inc(not_2_out_2), .Load(or_4_out_3), .Reset(ResetCPU),
    .Out(pcounter_1_out));
  Not not_3 (.in_1(or_3_out_3), .out_2(not_3_out_2));
  Clock clock_1 (.out_1(clock_1_out_1));
  And and_4 (.in_1(and_5_out_3), .in_2(s_r_ff_1_qn), .out_3(and_4_out_3[6]));
  And and_5 (.in_1(jogar), .in_2(not_5_out_2), .out_3(and_5_out_3));
  Not not_4 (.in_1(jogar), .out_2(not_4_out_2));
  Not not_5 (.in_1(Processando), .out_2(not_5_out_2));
  Dmux dmux_1 (.In(mux16_1_out_4[3]), .Sel(A_Register_out_3_2[14]), .A(dmux_1_a), .B(dmux_1_b));
  S_R_Flip_Flop s_r_ff_1 (
    .S(Processando), .clk(clock_1_out_1), .R(not_4_out_2), .Qn(s_r_ff_1_qn));  // open: Q, preset, reset, en
  Dmux dmux_2 (.In(dmux_1_b), .Sel(A_Register_out_3[13]), .A(dmux_2_a), .B(dmux_2_b));
  Mux16 mux16_4 (
    .A(alu_1_out),
    .B({{8{1'b0}}, Reset, and_4_out_3[6], _2Papel, _2Tesoura, _2Pedra, _1Papel, _1Tesoura, _1Pedra}),
    .Sel(and_4_out_3[6]), .out_4(mux16_4_out_4));
  Clock clock_2 (.out_1(clock_2_out_1));
  Clock clock_3 (.out_1(clock_3_out_1));
  Register register_1 (
    .in_1(mux16_4_out_4), .in_2(or_5_out_3),
    .out_3({register_1_out_3[15], Erro, VitoriaP2, Vitoria1, Pontuacao2, Pontuacao2_2, Pontuacao1, Pontuacao1_2, register_1_out_3[7], Processando, register_1_out_3[5:0]}));
  Or or_5 (.in_1(dmux_2_b), .in_2(and_4_out_3[6]), .out_3(or_5_out_3));
  RAM #(.addrWidth(14), .dataWidth(16), .bus("separate")) ram_1 (
    .addr(A_Register_out_3), .din(alu_1_out), .data(ram_1_data), .str(dmux_1_a), .clk(clock_2_out_1),
    .ld(1'b1));  // open: sel, clr
  RAM #(.addrWidth(13), .dataWidth(16), .bus("separate")) ram_2 (
    .addr(A_Register_out_3[12:0]), .din(alu_1_out), .data(ram_2_data), .str(dmux_2_a), .clk(clock_3_out_1),
    .ld(1'b1));  // open: sel, clr
  Mux16 mux16_5 (
    .A(ram_2_data),
    .B({register_1_out_3[15], Erro, VitoriaP2, Vitoria1, Pontuacao2, Pontuacao2_2, Pontuacao1, Pontuacao1_2, register_1_out_3[7], Processando, register_1_out_3[5:0]}),
    .Sel(A_Register_out_3[13]), .out_4(mux16_5_out_4));
  Mux16 mux16_6 (.A(ram_1_data), .B(mux16_5_out_4), .Sel(A_Register_out_3_2[14]), .out_4(mux16_6_out_4));

  // Notes on the sheet:
  //   contents of rom_1 (hex, n*v repeats v):
  //   6000 fc10 0 e308 40 e010 0 e302 3 ea88 4 ea88 0 fc10 80 e010 1c e302 1 ea88 2 ea88 3 ea88 4 ea88 e0
  //   ea87 1 fc10 300 e1d0 c4 e302 2 fc10 c00 e1d0 d8 e302 0 fc10 1 e010 30 e302 4 fdc8 0 fc10 2 e010 38
  //   e302 4 fdc8 0 fc10 4 e010 40 e302 4 fdc8 4 fc10 ea88 e390 4c e302 4000 ec10 3 e308 e0 ea87 0 fc10 8
  //   e010 54 e302 4 fdc8 0 fc10 10 e010 5c e302 4 fdc8 0 fc10 20 e010 64 e302 4 fdc8 4 fc10 1 e4d0 70
  //   e302 4000 ec10 3 e308 e0 ea87 0 fc10 1 e010 82 e305 0 fc10 2 e010 94 e305 0 fc10 4 e010 a6 e305 0
  //   fc10 8 e010 e0 e305 0 fc10 10 e010 b8 e305 0 fc10 20 e010 cc e305 0 fc10 8 e010 cc e305 0 fc10 10
  //   e010 e0 e305 0 fc10 20 e010 b8 e305 0 fc10 8 e010 b8 e305 0 fc10 10 e010 cc e305 0 fc10 20 e010 e0
  //   e305 1 fc10 100 e090 1 e308 1 fc10 300 e1d0 ca e305 3 fc10 1000 e090 3 e308 e0 ea87 2 fc10 400 e090
  //   2 e308 2 fc10 c00 e1d0 de e305 3 fc10 2000 e090 3 e308 e0 ea87 1 fc10 3 f088 2 fc10 3 f088 3 fc10
  //   6000 e308 0 ea87 ee ea87
endmodule

module HackPcJokenpo (
  input  ResetCPU,
  input  Reset,
  input  jogar,
  input  _2Papel,
  input  _2Tesoura,
  input  _2Pedra,
  input  _1Papel,
  input  _1Tesoura,
  input  _1Pedra,
  output Processando,
  output Erro,
  output VitoriaP2,
  output VitoriaP1,
  output PontuacaoJ2,
  output PontuacaoJ2_2,
  output PontuacaoJ1,
  output PontuacaoJ1_2
);

  DebugHackPC MaquinaJokenpo (
    .ResetCPU(ResetCPU), .Processando(Processando), .Erro(Erro), .VitoriaP2(VitoriaP2), .Vitoria1(VitoriaP1),
    .Pontuacao2(PontuacaoJ2), .Pontuacao2_2(PontuacaoJ2_2), .Pontuacao1(PontuacaoJ1),
    .Pontuacao1_2(PontuacaoJ1_2), .Reset(Reset), .jogar(jogar), ._2Papel(_2Papel), ._2Tesoura(_2Tesoura),
    ._2Pedra(_2Pedra), ._1Papel(_1Papel), ._1Tesoura(_1Tesoura), ._1Pedra(_1Pedra));
endmodule
