// Logisim project NTT_Memory.circ as structural Verilog
// NTT_DFF
module DFF (
  input  In,
  output Out
);

  wire clock_1_out_1, nand_1_out, nand_2_out, nand_4_out, not_1_out_2;

  Clock clock_1 (.out_1(clock_1_out_1));
  Not not_1 (.in_1(In), .out_2(not_1_out_2));
  nand nand_1 (nand_1_out, In, clock_1_out_1);
  nand nand_2 (nand_2_out, clock_1_out_1, not_1_out_2);
  nand nand_3 (Out, nand_1_out, nand_4_out);
  nand nand_4 (nand_4_out, Out, nand_2_out);
endmodule

// NTT_Bit
module Bit (
  input  In,
  input  Load,
  output Out
);

  wire clock_1_out_1, mux_1_out_4;

  Clock clock_1 (.out_1(clock_1_out_1));
  D_Flip_Flop d_ff_1 (.clk(clock_1_out_1), .D(mux_1_out_4), .Q(Out));  // open: Qn, preset, en, reset
  Mux mux_1 (.A(Out), .B(In), .Sel(Load), .out_4(mux_1_out_4));
endmodule

// NTT_Register
module Register (
  input  [15:0] in_1,
  input  in_2,
  output [15:0] out_3
);

  Bit bit_1 (.In(in_1[0]), .Load(in_2), .Out(out_3[0]));
  Bit bit_2 (.In(in_1[1]), .Load(in_2), .Out(out_3[1]));
  Bit bit_3 (.In(in_1[2]), .Load(in_2), .Out(out_3[2]));
  Bit bit_4 (.In(in_1[3]), .Load(in_2), .Out(out_3[3]));
  Bit bit_5 (.In(in_1[4]), .Load(in_2), .Out(out_3[4]));
  Bit bit_6 (.In(in_1[5]), .Load(in_2), .Out(out_3[5]));
  Bit bit_7 (.In(in_1[6]), .Load(in_2), .Out(out_3[6]));
  Bit bit_8 (.In(in_1[7]), .Load(in_2), .Out(out_3[7]));
  Bit bit_9 (.In(in_1[8]), .Load(in_2), .Out(out_3[8]));
  Bit bit_10 (.In(in_1[9]), .Load(in_2), .Out(out_3[9]));
  Bit bit_11 (.In(in_1[10]), .Load(in_2), .Out(out_3[10]));
  Bit bit_12 (.In(in_1[11]), .Load(in_2), .Out(out_3[11]));
  Bit bit_13 (.In(in_1[12]), .Load(in_2), .Out(out_3[12]));
  Bit bit_14 (.In(in_1[13]), .Load(in_2), .Out(out_3[13]));
  Bit bit_15 (.In(in_1[14]), .Load(in_2), .Out(out_3[14]));
  Bit bit_16 (.In(in_1[15]), .Load(in_2), .Out(out_3[15]));
endmodule

// NTT_RAM8
module RAM8 (
  input  [15:0] In,
  input  Load,
  input  [2:0] Addr,
  output [15:0] Out
);

  wire dmux8way_1_out_5, dmux8way_1_out_6, dmux8way_1_out_7, dmux8way_1_out_8, dmux8way_1_out_9,
       dmux8way_1_out_10, dmux8way_1_out_11, dmux8way_1_out_12;
  wire [15:0] register_1_out_3, register_2_out_3, register_3_out_3, register_4_out_3, register_5_out_3,
       register_6_out_3, register_7_out_3, register_8_out_3;

  DMux8Way dmux8way_1 (
    .in_1(Load), .in_3(Addr[0]), .in_4(Addr[1]), .in_2(Addr[2]), .out_5(dmux8way_1_out_5),
    .out_6(dmux8way_1_out_6), .out_7(dmux8way_1_out_7), .out_8(dmux8way_1_out_8), .out_9(dmux8way_1_out_9),
    .out_10(dmux8way_1_out_10), .out_11(dmux8way_1_out_11), .out_12(dmux8way_1_out_12));
  Register register_1 (.in_1(In), .in_2(dmux8way_1_out_5), .out_3(register_1_out_3));
  Register register_2 (.in_1(In), .in_2(dmux8way_1_out_6), .out_3(register_2_out_3));
  Register register_3 (.in_1(In), .in_2(dmux8way_1_out_7), .out_3(register_3_out_3));
  Register register_4 (.in_1(In), .in_2(dmux8way_1_out_8), .out_3(register_4_out_3));
  Register register_5 (.in_1(In), .in_2(dmux8way_1_out_9), .out_3(register_5_out_3));
  Register register_6 (.in_1(In), .in_2(dmux8way_1_out_10), .out_3(register_6_out_3));
  Register register_7 (.in_1(In), .in_2(dmux8way_1_out_11), .out_3(register_7_out_3));
  Register register_8 (.in_1(In), .in_2(dmux8way_1_out_12), .out_3(register_8_out_3));
  Mux8Way16 mux8way16_1 (
    .A(register_1_out_3), .B(register_2_out_3), .C(register_3_out_3), .D(register_4_out_3),
    .E(register_5_out_3), .F(register_6_out_3), .G(register_7_out_3), .H(register_8_out_3), .in_5(Addr[0]),
    .in_6(Addr[1]), .in_8(Addr[2]), .out_12(Out));
endmodule

// NTT_RAM64
module RAM64 (
  input  [15:0] In,
  input  Load,
  input  [5:0] Addr,
  output [15:0] Out
);

  wire clock_1_out_1, clock_2_out_1, clock_3_out_1, clock_4_out_1, clock_5_out_1, clock_6_out_1,
       clock_7_out_1, clock_8_out_1, dmux8way_1_out_5, dmux8way_1_out_6, dmux8way_1_out_7, dmux8way_1_out_8,
       dmux8way_1_out_9, dmux8way_1_out_10, dmux8way_1_out_11, dmux8way_1_out_12;
  wire [15:0] ram_1_data, ram_2_data, ram_3_data, ram_4_data, ram_5_data, ram_6_data, ram_7_data, ram_8_data;

  DMux8Way dmux8way_1 (
    .in_1(Load), .in_3(Addr[3]), .in_4(Addr[4]), .in_2(Addr[5]), .out_5(dmux8way_1_out_5),
    .out_6(dmux8way_1_out_6), .out_7(dmux8way_1_out_7), .out_8(dmux8way_1_out_8), .out_9(dmux8way_1_out_9),
    .out_10(dmux8way_1_out_10), .out_11(dmux8way_1_out_11), .out_12(dmux8way_1_out_12));
  Clock clock_1 (.out_1(clock_1_out_1));
  Clock clock_2 (.out_1(clock_2_out_1));
  Clock clock_3 (.out_1(clock_3_out_1));
  Clock clock_4 (.out_1(clock_4_out_1));
  Clock clock_5 (.out_1(clock_5_out_1));
  Clock clock_6 (.out_1(clock_6_out_1));
  Clock clock_7 (.out_1(clock_7_out_1));
  Clock clock_8 (.out_1(clock_8_out_1));
  RAM #(.addrWidth(3), .dataWidth(16), .bus("separate")) ram_1 (
    .addr(Addr[2:0]), .din(In), .data(ram_1_data), .str(dmux8way_1_out_5), .clk(clock_1_out_1), .ld(1'b1));  // open: sel, clr
  RAM #(.addrWidth(3), .dataWidth(16), .bus("separate")) ram_2 (
    .addr(Addr[2:0]), .din(In), .data(ram_2_data), .str(dmux8way_1_out_6), .clk(clock_2_out_1), .ld(1'b1));  // open: sel, clr
  RAM #(.addrWidth(3), .dataWidth(16), .bus("separate")) ram_3 (
    .addr(Addr[2:0]), .din(In), .data(ram_3_data), .str(dmux8way_1_out_7), .clk(clock_3_out_1), .ld(1'b1));  // open: sel, clr
  RAM #(.addrWidth(3), .dataWidth(16), .bus("separate")) ram_4 (
    .addr(Addr[2:0]), .din(In), .data(ram_4_data), .str(dmux8way_1_out_8), .clk(clock_4_out_1), .ld(1'b1));  // open: sel, clr
  RAM #(.addrWidth(3), .dataWidth(16), .bus("separate")) ram_5 (
    .addr(Addr[2:0]), .din(In), .data(ram_5_data), .str(dmux8way_1_out_9), .clk(clock_5_out_1), .ld(1'b1));  // open: sel, clr
  RAM #(.addrWidth(3), .dataWidth(16), .bus("separate")) ram_6 (
    .addr(Addr[2:0]), .data(ram_6_data), .str(dmux8way_1_out_10), .clk(clock_6_out_1), .ld(1'b1));  // open: din, sel, clr
  RAM #(.addrWidth(3), .dataWidth(16), .bus("separate")) ram_7 (
    .addr(Addr[2:0]), .din(In), .data(ram_7_data), .str(dmux8way_1_out_11), .clk(clock_7_out_1), .ld(1'b1));  // open: sel, clr
  RAM #(.addrWidth(3), .dataWidth(16), .bus("separate")) ram_8 (
    .addr(Addr[2:0]), .din(In), .data(ram_8_data), .str(dmux8way_1_out_12), .clk(clock_8_out_1), .ld(1'b1));  // open: sel, clr
  Mux8Way16 mux8way16_1 (
    .A(ram_1_data), .B(ram_2_data), .C(ram_3_data), .D(ram_4_data), .E(ram_5_data), .F(ram_6_data),
    .G(ram_7_data), .H(ram_8_data), .in_5(Addr[3]), .in_6(Addr[4]), .in_8(Addr[5]), .out_12(Out));
endmodule

// NTT_RAM16K
module RAM16k (
  input  Load,
  input  [13:0] Addr,
  input  [15:0] In,
  output [15:0] Out
);

  wire clock_1_out_1;

  Clock clock_1 (.out_1(clock_1_out_1));
  RAM #(.addrWidth(14), .dataWidth(16), .bus("separate")) ram_1 (
    .addr(Addr), .din(In), .data(Out), .str(Load), .clk(clock_1_out_1), .ld(1'b1));  // open: sel, clr
endmodule

// NTT_PCounter
module PCounter (
  input  Inc,
  input  Load,
  input  Reset,
  input  [15:0] In,
  output [15:0] Out
);

  wire [15:0] inc16_1_out_2, mux16_1_out_4, mux16_2_out_4, mux16_3_out_4;

  Mux16 mux16_1 (.A(mux16_2_out_4), .B({16{1'b0}}), .Sel(Reset), .out_4(mux16_1_out_4));
  Mux16 mux16_2 (.A(mux16_3_out_4), .B(In), .Sel(Load), .out_4(mux16_2_out_4));
  Mux16 mux16_3 (.A(Out), .B(inc16_1_out_2), .Sel(Inc), .out_4(mux16_3_out_4));
  Inc16 inc16_1 (.in_1(Out), .out_2(inc16_1_out_2));
  Register register_1 (.in_1(mux16_1_out_4), .in_2(1'b1), .out_3(Out));
endmodule

// NTT_Clock
module Clock (
  output out_1
);

  Clock_part clock_1 (.out(out_1));
endmodule
